// Logisim project Decoder.circ as structural Verilog: 1 circuit, main circuit main
module main (
  input  in_1,
  input  in_2,
  input  [1:0] in_3,
  output out_4,
  output out_5,
  output out_6,
  output out_7,
  output out_8,
  output out_9,
  output out_10,
  output out_11
);

  wire not_1_out, not_2_out;

  not not_1 (not_1_out, in_1);
  not not_2 (not_2_out, in_2);
  and and_1 (out_5, not_1_out, not_2_out);
  and and_2 (out_8, in_1, not_2_out);
  and and_3 (out_10, in_2, not_1_out);
  and and_4 (out_11, in_2, in_1);
  Decoder #(.select(2)) decoder_1 (.out0(out_4), .out1(out_6), .out2(out_7), .out3(out_9), .sel(in_3));  // open: en
endmodule
