// Logisim project Memory.circ as structural Verilog: 1 circuit, main circuit main
module main (
  input  [1:0] A,
  input  D2,
  input  WE
);

  wire and_1_out, and_2_out, and_3_out, and_4_out, decoder_1_out0, decoder_1_out1, decoder_1_out2,
       decoder_1_out3;

  Decoder #(.select(2)) decoder_1 (
    .out0(decoder_1_out0), .out1(decoder_1_out1), .out2(decoder_1_out2), .out3(decoder_1_out3), .sel(A));  // open: en
  and and_1 (and_1_out, decoder_1_out0, WE);
  and and_2 (and_2_out, decoder_1_out1, WE);
  and and_3 (and_3_out, decoder_1_out2, WE);
  and and_4 (and_4_out, decoder_1_out3, WE);
  Multiplexer multiplexer_1 ();  // open: in0, in1, out, sel, en
  Register #(.width(1)) register_1 (.D(D2), .en(and_1_out));  // open: Q, clk, clr
  Register #(.width(1)) register_2 (.D(D2), .en(and_2_out));  // open: Q, clk, clr
  Register #(.width(1)) register_3 (.D(D2), .en(and_3_out));  // open: Q, clk, clr
  Register #(.width(1)) register_4 (.D(D2), .en(and_4_out));  // open: Q, clk, clr
endmodule
