// Logisim project Multiplexer.circ as structural Verilog: 1 circuit, main circuit main
module main (
  input  in_1,
  input  in_2,
  input  in_3,
  input  in_4,
  input  in_5,
  input  in_6,
  output out_7,
  output out_8
);

  wire and_1_out, and_2_out, not_1_out;

  not not_1 (not_1_out, in_2);
  and and_1 (and_1_out, in_1, not_1_out);
  and and_2 (and_2_out, in_2, in_3);
  Multiplexer multiplexer_1 (.in0(in_4), .in1(in_5), .out(out_8), .sel(in_6), .en(in_6));
  or or_1 (out_7, and_1_out, and_2_out);
endmodule
