// Logisim project Register.circ as structural Verilog: 1 circuit, main circuit main
module main (
  input  in_1,
  input  in_2,
  input  in_3,
  input  in_4,
  input  in_5,
  input  [3:0] in_6,
  input  in_7,
  output out_8,
  output out_9,
  output out_10,
  output out_11,
  output [3:0] out_12
);

  wire and_1_out, and_2_out, and_3_out, and_4_out, and_5_out, and_6_out, and_7_out, and_8_out, and_9_out,
       and_10_out, and_11_out, and_12_out, and_13_out, and_14_out, and_15_out, and_16_out, not_1_out,
       not_2_out, not_3_out, not_4_out, not_6_out, not_7_out, not_8_out, not_9_out, not_11_out, not_12_out,
       not_13_out, not_14_out, not_16_out, not_17_out, not_18_out, not_19_out;

  not not_1 (not_1_out, in_1);
  and and_1 (and_1_out, in_5, not_1_out);
  not not_2 (not_2_out, and_1_out);
  and and_2 (and_2_out, not_2_out, out_8);
  not not_3 (not_3_out, and_2_out);
  and and_3 (and_3_out, in_1, in_5);
  not not_4 (not_4_out, and_3_out);
  and and_4 (and_4_out, not_3_out, not_4_out);
  not not_5 (out_8, and_4_out);
  and and_5 (and_5_out, in_5, not_8_out);
  not not_6 (not_6_out, and_5_out);
  and and_6 (and_6_out, not_6_out, out_9);
  not not_7 (not_7_out, and_6_out);
  Register #(.width(4)) register_1 (.D(in_6), .en(in_7), .Q(out_12), .clk(in_7));  // open: clr
  not not_8 (not_8_out, in_2);
  and and_7 (and_7_out, in_2, in_5);
  not not_9 (not_9_out, and_7_out);
  and and_8 (and_8_out, not_7_out, not_9_out);
  not not_10 (out_9, and_8_out);
  not not_11 (not_11_out, in_3);
  and and_9 (and_9_out, in_5, not_11_out);
  not not_12 (not_12_out, and_9_out);
  and and_10 (and_10_out, not_12_out, out_10);
  not not_13 (not_13_out, and_10_out);
  and and_11 (and_11_out, in_3, in_5);
  not not_14 (not_14_out, and_11_out);
  and and_12 (and_12_out, not_13_out, not_14_out);
  not not_15 (out_10, and_12_out);
  not not_16 (not_16_out, in_4);
  and and_13 (and_13_out, in_5, not_16_out);
  not not_17 (not_17_out, and_13_out);
  and and_14 (and_14_out, not_17_out, out_11);
  not not_18 (not_18_out, and_14_out);
  and and_15 (and_15_out, in_4, in_5);
  not not_19 (not_19_out, and_15_out);
  and and_16 (and_16_out, not_18_out, not_19_out);
  not not_20 (out_11, and_16_out);
endmodule
